// Digital circuit CORE.dig as structural Verilog
module CORE (
  input  clk,
  input  RST,
  input  CLR,
  input  in_4,
  input  [11:0] MIPCBI,
  input  [15:0] PCBI,
  input  MIPCBE,
  input  PCBE
);

  wire ALUD_CO, ALUDH_OE, ALUDL_OE, ALUS_OE, and_3_out, and_4_out, ASSERT_p5, BR_Q, button_1_out, CLK_t,
       CLKR, comparator_1_eq, comparator_1_gt, comparator_1_lt, comparator_2_eq, comparator_3_eq, DC_JUMP,
       DIRECT_OE, DIRECT_WE, DUMP_p6, EXT_p5, IMMED_OE, IRQ_OE, or_1_out, RAM_OE, RAM_WE, RF_HWE, RF_LWE,
       RF_SFR, RFSRCR_WE, ROM_OE, SFR_OE, SR_WE, WR_WE, XRAM_OE, XRAM_WE;
  wire [2:0] BR_SRC, BUS_SRC, JUMP_TYPE;
  wire [3:0] ALUSD_FUNC, multiplexer_2_out, RF_SRC;
  wire [5:4] multiplexer_2_out_2;
  wire [6:0] and_2_out;
  wire [7:0] BUS_D, IMMED, RF_Q;
  wire [7:4] RFSRCR_q;
  wire [11:0] ADDRESS, MIPC;
  wire [15:0] ADDR_16, PCER_q;
  wire [47:45] DECODER_2_d;

  Decoder #(.Selector_Bits(3)) decoder_1 (
    .sel(BUS_SRC), .out_0(ALUS_OE), .out_1(ALUDL_OE), .out_2(ALUDH_OE), .out_3(IMMED_OE), .out_4(RAM_OE),
    .out_5(XRAM_OE), .out_6(ROM_OE), .out_7(IRQ_OE));
  DCOUTER #(.generic("Bits := 12;")) dcouter_1 (
    .CLK(CLK_t), .CLR(CLR), .CNT(1'b1), .LE(DC_JUMP), .D(ADDRESS), .Q(MIPC));
  Comparator #(.Bits(8)) comparator_1 (
    .a(RF_Q), .b(IMMED), .gt(comparator_1_gt), .eq(comparator_1_eq), .lt(comparator_1_lt));
  assign BUS_D = IMMED_OE ? IMMED : 8'bz;  // Driver driver_1
  assign BUS_D = SFR_OE ? RF_Q : 8'bz;  // Driver driver_2
  // Probe on BUS_D
  PullDown #(.Bits(8)) pulldown_1 (.out(BUS_D));
  PCE PCER (.CLK(CLK_t), .D(BUS_D), .RS(RF_SRC), .LWE(RF_LWE), .HWE(RF_HWE), .Q(PCER_q));
  Multiplexer #(.Selector_Bits(3)) multiplexer_1 (
    .sel(JUMP_TYPE), .in_0(1'b0), .in_1(1'b1), .in_2(comparator_1_gt), .in_3(comparator_1_eq),
    .in_4(comparator_1_lt), .in_5(BR_Q), .in_6(RST), .in_7(1'b0), .out(DC_JUMP));
  ROM #(.AddrBits(12), .Bits(48)) DECODER_2 (
    .A(MIPC), .sel(1'b1),
    .D({DECODER_2_d, IMMED, ADDRESS, JUMP_TYPE, ALUSD_FUNC, XRAM_WE, RAM_WE, RFSRCR_WE, BR_SRC, SR_WE, WR_WE, BUS_SRC, RF_SFR, RF_HWE, RF_LWE, RF_SRC}));
  Register #(.Bits(8)) RFSRCR (.D(BUS_D), .C(CLK_t), .en(RFSRCR_WE), .Q({RFSRCR_q, and_2_out[3:0]}));
  and and_1 (and_2_out[5], RFSRCR_q[4], RAM_WE);
  and and_2 (and_2_out[6], RFSRCR_q[4], RAM_OE);
  Comparator #(.Bits(12)) comparator_2 (.a(MIPCBI), .b(MIPC), .eq(comparator_2_eq));  // open: gt, lt
  Comparator #(.Bits(16)) comparator_3 (.a(PCBI), .b(PCER_q), .eq(comparator_3_eq));  // open: gt, lt
  and and_3 (and_3_out, comparator_2_eq, MIPCBE);
  and and_4 (and_4_out, comparator_3_eq, PCBE);
  Multiplexer #(.Bits(7)) multiplexer_2 (
    .sel(RF_SFR), .in_0({1'b0, RF_HWE, RF_LWE, RF_SRC}),
    .in_1({and_2_out[6:5], and_2_out[5], and_2_out[3:0]}),
    .out({SFR_OE, multiplexer_2_out_2, multiplexer_2_out}));
  // Probe on MIPC
  // Probe on RF_SRC
  // Probe on RF_LWE
  // Probe on RF_HWE
  // Probe on RF_SFR
  // Probe on BUS_SRC
  // Probe on WR_WE
  // Probe on SR_WE
  // Probe on BR_SRC
  // Probe on RFSRCR_WE
  // Probe on RAM_WE
  // Probe on XRAM_WE
  // Probe on ALUSD_FUNC
  // Probe on JUMP_TYPE
  // Probe on ADDRESS
  // Probe on IMMED
  // ASSERT ASSERT: pin names not known; wires that end beside it: CLK_t, BUS_D, ADDR_16[15:8], DIRECT_WE, ASSERT_p5
  Button button_1 (.out(button_1_out));
  // reg_file RF: pin names not known; wires that end beside it: CLK_t, multiplexer_2_out, BUS_D, multiplexer_2_out_2[4], multiplexer_2_out_2[5], RF_Q
  // EXTCTL EXT: pin names not known; wires that end beside it: DIRECT_WE, ADDR_16[15:8], BUS_D, CLK_t, EXT_p5
  // SwitchDT switchdt_1: pin names not known; wires that end beside it: clk, button_1_out, CLKR
  // Probe on RF_Q
  // Probe on EXT_p5
  or or_1 (or_1_out, ASSERT_p5, and_3_out, and_4_out);
  reg__sync_clear #(.generic("Bits := 8;")) WR (.D(BUS_D), .CLK(CLK_t), .CLR(CLR), .LE(WR_WE), .Q(ADDR_16[7:0]));
  reg__sync_clear #(.generic("Bits := 8;")) SR (.D(BUS_D), .CLK(CLK_t), .CLR(CLR), .LE(SR_WE), .Q(ADDR_16[15:8]));
  and and_5 (DIRECT_WE, RF_SFR, RAM_WE);
  and and_6 (DIRECT_OE, RF_SFR, RAM_OE);
  // DUMP DUMP: pin names not known; wires that end beside it: DIRECT_WE, ADDR_16[15:8], BUS_D, CLK_t, CLK_t, DUMP_p6
  STALL STALL (.C(CLKR), .AC(or_1_out), .S(in_4), .OAC(CLK_t));  // open: G, nCLR, O
  // Probe on DUMP_p6
  // Probe on ADDR_16[7:0]
  // Probe on ADDR_16[15:8]
  ALU ALU (
    .A(RF_Q), .B(ADDR_16[7:0]), .S(ALUSD_FUNC), .CI(BR_Q), .SOE(ALUS_OE), .DOE(ALUDL_OE), .FOE(ALUDH_OE),
    .O(BUS_D), .ALUDF(ALUD_CO));
  ROM #(.AddrBits(16), .Bits(8)) ROM (.A(ADDR_16), .sel(ROM_OE), .D(BUS_D));
  RAM RAM (.AC(CLK_t), .A(ADDR_16[15:8]), .WE(RAM_WE), .nOE(RAM_OE), .Dt(RF_SFR), .O(BUS_D));
  RAMSinglePortSel #(.AddrBits(16), .isProgramMemory("true"), .Bits(8)) XRAM (
    .A(ADDR_16), .CS(~1'b0), .WE(XRAM_WE), .OE(XRAM_OE), .D(BUS_D));
  BR BR (.CLK(CLK_t), .nCLR(CLR), .S(BR_SRC), .I4(ALUD_CO), .I5(ALUD_CO), .I7(RF_Q[0]), .I6(RF_Q[7]), .Q(BR_Q));

  // Other names for the same wires on the sheet: ADDR_RAM[7:0] = ADDR_16[15:8]; GO = in_4

  // Notes on the sheet:
  //   clk: Hz: 2147483647
  //   contents of DECODER_2 (hex, n*v repeats v):
  //   711900488,100889,33a,105106,3830b5,3c54b8,3c08b9,1003cb00000a,18016300000a,1c008700000a,
  //   1e004f00000a,1f001f00000a,100485,34088a,6e0510086,1e803b00000a,1ec02b00000a,100485,
  //   30088a,a00,6e0510086,1ea03900000a,b3c,c800c,100486,1530c0,3c50b8,6e07c00b9,6e0780136,
  //   1e404700000a,100485,30088a,600,980,6e0520086,1e06c880000a,100481,100882,6e0520086,
  //   1d005700000a,100485,34088a,6e0400236,1c807300000a,1cc06300000a,100485,30088a,a00,
  //   6e0400236,1ca07100000a,b3c,c800c,640,1430b6,3c50b8,6e07c00b9,6e04001b6,1c407f00000a,
  //   100485,30088a,600,980,6e04002b6,1c06bc80000a,100481,100882,6e04002b6,1a010300000a,
  //   1b00a100000a,33c,100485,34088a,23d,25003d,26dd00300d,10348c,850b8,3c20b9,658c,6e04c00b9,
  //   1a80d300000a,1ac0b500000a,100485,30088a,a00,23c,100486,1d008c,10048c,6e05c00b6,1aa0c900000a,
  //   b3c,c800c,640,1400bd,24043d,1500c0,26d900358d,3c54b8,3c07c08b9,405,450b6,d1403000,
  //   6e0400000,6e0700035,1a40ef00000a,1a60db00000a,3000,6e0700035,73c,1400bd,2c003d,28083c,
  //   c800c,3640,18048d,1530c0,3c50b8,6e07c00b9,1a06c880000a,33c,100880,600,10088c,c800c,
  //   1500c0,243030,3c50b8,6e07c00b9,19010f00000a,100485,34088a,600,110086,6e05400b6,18813700000a,
  //   18c11f00000a,100485,30088a,a00,100486,236,6e0550080,18a13500000a,b3c,c800c,640,1400bc,
  //   100486,1500c0,10048c,1430b6,3c50b8,6e07c00b9,6e07c0036,18415300000a,18613f00000a,
  //   2000,6e0700035,73c,1400bd,2c003d,28083c,c800c,2640,18048d,1530c0,3c50b8,6e07c00b9,
  //   1806bc80000a,b3c,c800c,640,200830,153080,3c50b8,6e07c00b9,1402dd00000a,1601fb00000a,
  //   17017f00000a,33d,100485,34088a,23c,10248d,c54bc,300035,14510c,26d9403580,3c54b8,3c07c08b9,
  //   1681c100000a,16c19b00000a,33d,100485,30088a,a00,23c,10248d,c54bc,300035,14510c,26d9403580,
  //   3c54b8,3c07c08b9,16a1b100000a,b3c,c800c,2640,c5486,300035,1400bc,14510c,26d9403580,
  //   3c54b8,3c07c08b9,2700,c5486,300035,1400bc,14510c,26d9403580,3c54b8,3c07c08b9,1641e100000a,
  //   1661c900000a,385105,6e0700035,73c,1400bd,2c003d,28083c,c800c,640,1c510d,1000,18048d,
  //   1530c0,3c50b8,6e07c00b9,1606c880000a,73c,1400bd,2c003d,28083c,c800c,640,1c013d,38050d,
  //   345105,303035,3c50b8,6e07c00b9,15020f00000a,b3c,c800c,640,1400bc,100485,34088a,11308c,
  //   3c50b8,6e07c00b9,1482a500000a,14c22700000a,b3c,c800c,640,1400bc,100485,30088a,a00,
  //   11308c,3c50b8,6e07c00b9,14a22900000a,21bc,227b187036,82407,850bc,18703c,18203d,2281187036,
  //   82407,850bc,18703c,18203d,2285187036,82407,850bc,18703c,18203d,2289187036,82407,850bc,
  //   18703c,18203d,228d187036,82407,850bc,18703c,18203d,2291187036,82407,850bc,18703c,
  //   18203d,2295187036,82407,850bc,18703c,18203d,2299187036,82407,850bc,18743c,29c58203d,
  //   1b6,21b7,6e0740035,18703c,18203d,18703c,18203d,18703c,18203d,18703c,18203d,18703c,
  //   18203d,18703c,18203d,18743c,18203d,1450b7,10148d,1400b6,6e0740035,1442c300000a,1462af00000a,
  //   3000,3c50b1,6e07c00b2,73c,1400bd,2c003d,28083c,c800c,640,1c510d,303035,3c50b8,6e07c00b9,
  //   1406bc80000a,73c,1400bd,2c003d,28083c,c800c,640,1c013d,38050d,305105,303035,3c50b8,
  //   6e07c00b9,12035f00000a,1302f300000a,106485,34088a,63d,c0506,1400bc,40c,2400b5,10048d,
  //   6e04c00b6,12833300000a,12c30b00000a,106485,30088a,a00,63d,c0506,1400bc,40c,2400b5,
  //   10048d,6e04c00b6,12a32300000a,6005,b3c,c800c,640,1400bd,c0506,1400bc,40c,2400b5,10048d,
  //   6dc4c30b6,6005,73d,c0506,1400bc,40c,2400b5,10048d,6dc4c30b6,12435500000a,12633f00000a,
  //   102486,85481,3c0882,6e0400336,6005,73c,1400bd,2c003d,28083c,c800c,640,18048d,1530c0,
  //   3c50b8,6e07c00b9,1206c880000a,3332,3c54b8,3c08b9,6dc403331,11036f00000a,33c,100485,
  //   34088a,600,c800c,10088c,6dc5530c0,10839d00000a,10c38700000a,33c,100485,30088a,a00,
  //   600,c800c,10088c,1530c0,3c50b8,6e07c00b9,10a39d00000a,b3c,c800c,640,1430bd,3c54b8,
  //   3c08b9,b3c,10048d,c800c,6dc5530c0,1043bf00000a,1063a900000a,102486,85488,3c0889,6e0400336,
  //   73c,1400bd,2c003d,28083c,c800c,640,1c050d,345105,303035,3c50b8,6e07c00b9,1006bc80000a,
  //   373c,850b8,3c20b9,658c,6e04c00b9,8052700000a,c047f00000a,e042f00000a,f03db00000a,
  //   33c,100485,34088a,6dc51308c,e83fb00000a,ec3e900000a,33c,100485,30088a,a00,6dc51308c,
  //   ea3f900000a,333c,3c54b8,3c08b9,700,c800c,10088c,6dc5530c0,6dc403336,e441f00000a,e640900000a,
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  //   contents of ROM (hex, n*v repeats v):
  //   75,81,0,75,82,0,75,83,0,75,d0,0,75,e0,0,75,f0,0,75,e0,1,75,f0,0,84,85,d0,fd,75,fe,
  //   5,75,ff,2,75,e0,9,75,f0,18,84,85,e0,fd,75,fe,0,75,ff,2,85,f0,fd,75,fe,9,75,ff,2,85,
  //   d0,fd,75,fe,0,75,ff,2,75,fb,1,75,e0,0,75,f0,0,84,85,d0,fd,75,fe,4,75,ff,2,75,e0,0,
  //   75,f0,1,84,85,e0,fd,75,fe,0,75,ff,2,85,f0,fd,75,fe,0,75,ff,2,85,d0,fd,75,fe,0,75,
  //   ff,2,75,e0,0,75,f0,2,84,85,e0,fd,75,fe,0,75,ff,2,85,f0,fd,75,fe,0,75,ff,2,85,d0,fd,
  //   75,fe,0,75,ff,2,75,e0,0,75,f0,3,84,85,e0,fd,75,fe,0,75,ff,2,85,f0,fd,75,fe,0,75,ff,
  //   2,85,d0,fd,75,fe,0,75,ff,2,75,e0,0,75,f0,7c,84,85,e0,fd,75,fe,0,75,ff,2,85,f0,fd,
  //   75,fe,0,75,ff,2,85,d0,fd,75,fe,0,75,ff,2,75,e0,0,75,f0,7d,84,85,e0,fd,75,fe,0,75,
  //   ff,2,85,f0,fd,75,fe,0,75,ff,2,85,d0,fd,75,fe,0,75,ff,2,75,e0,0,75,f0,7e,84,85,e0,
  //   fd,75,fe,0,75,ff,2,85,f0,fd,75,fe,0,75,ff,2,85,d0,fd,75,fe,0,75,ff,2,75,e0,0,75,f0,
  //   7f,84,85,e0,fd,75,fe,0,75,ff,2,85,f0,fd,75,fe,0,75,ff,2,85,d0,fd,75,fe,0,75,ff,2,
  //   75,e0,0,75,f0,80,84,85,e0,fd,75,fe,0,75,ff,2,85,f0,fd,75,fe,0,75,ff,2,85,d0,fd,75,
  //   fe,0,75,ff,2,75,e0,0,75,f0,81,84,85,e0,fd,75,fe,0,75,ff,2,85,f0,fd,75,fe,0,75,ff,
  //   2,85,d0,fd,75,fe,0,75,ff,2,75,e0,0,75,f0,82,84,85,e0,fd,75,fe,0,75,ff,2,85,f0,fd,
  //   75,fe,0,75,ff,2,85,d0,fd,75,fe,0,75,ff,2,75,e0,0,75,f0,83,84,85,e0,fd,75,fe,0,75,
  //   ff,2,85,f0,fd,75,fe,0,75,ff,2,85,d0,fd,75,fe,0,75,ff,2,75,e0,0,75,f0,fc,84,85,e0,
  //   fd,75,fe,0,75,ff,2,85,f0,fd,75,fe,0,75,ff,2,85,d0,fd,75,fe,0,75,ff,2,75,e0,0,75,f0,
  //   fd,84,85,e0,fd,75,fe,0,75,ff,2,85,f0,fd,75,fe,0,75,ff,2,85,d0,fd,75,fe,0,75,ff,2,
  //   75,e0,0,75,f0,fe,84,85,e0,fd,75,fe,0,75,ff,2,85,f0,fd,75,fe,0,75,ff,2,85,d0,fd,75,
  //   fe,0,75,ff,2,75,e0,0,75,f0,ff,84,85,e0,fd,75,fe,0,75,ff,2,85,f0,fd,75,fe,0,75,ff,
  //   2,85,d0,fd,75,fe,0,75,ff,2,75,e0,1,75,f0,0,84,85,d0,fd,75,fe,5,75,ff,2,75,e0,1,75,
  //   f0,1,84,85,e0,fd,75,fe,1,75,ff,2,85,f0,fd,75,fe,0,75,ff,2,85,d0,fd,75,fe,1,75,ff,
  //   2,75,e0,1,75,f0,2,84,85,e0,fd,75,fe,0,75,ff,2,85,f0,fd,75,fe,1,75,ff,2,85,d0,fd,75,
  //   fe,0,75,ff,2,75,e0,1,75,f0,3,84,85,e0,fd,75,fe,0,75,ff,2,85,f0,fd,75,fe,1,75,ff,2,
  //   85,d0,fd,75,fe,0,75,ff,2,75,e0,1,75,f0,7c,84,85,e0,fd,75,fe,0,75,ff,2,85,f0,fd,75,
  //   fe,1,75,ff,2,85,d0,fd,75,fe,0,75,ff,2,75,e0,1,75,f0,7d,84,85,e0,fd,75,fe,0,75,ff,
  //   2,85,f0,fd,75,fe,1,75,ff,2,85,d0,fd,75,fe,0,75,ff,2,75,e0,1,75,f0,7e,84,85,e0,fd,
  //   75,fe,0,75,ff,2,85,f0,fd,75,fe,1,75,ff,2,85,d0,fd,75,fe,0,75,ff,2,75,e0,1,75,f0,7f,
  //   84,85,e0,fd,75,fe,0,75,ff,2,85,f0,fd,75,fe,1,75,ff,2,85,d0,fd,75,fe,0,75,ff,2,75,
  //   e0,1,75,f0,80,84,85,e0,fd,75,fe,0,75,ff,2,85,f0,fd,75,fe,1,75,ff,2,85,d0,fd,75,fe,
  //   0,75,ff,2,75,e0,1,75,f0,81,84,85,e0,fd,75,fe,0,75,ff,2,85,f0,fd,75,fe,1,75,ff,2,85,
  //   d0,fd,75,fe,0,75,ff,2,75,e0,1,75,f0,82,84,85,e0,fd,75,fe,0,75,ff,2,85,f0,fd,75,fe,
  //   1,75,ff,2,85,d0,fd,75,fe,0,75,ff,2,75,e0,1,75,f0,83,84,85,e0,fd,75,fe,0,75,ff,2,85,
  //   f0,fd,75,fe,1,75,ff,2,85,d0,fd,75,fe,0,75,ff,2,75,e0,1,75,f0,fc,84,85,e0,fd,75,fe,
  //   0,75,ff,2,85,f0,fd,75,fe,1,75,ff,2,85,d0,fd,75,fe,0,75,ff,2,75,e0,1,75,f0,fd,84,85,
  //   e0,fd,75,fe,0,75,ff,2,85,f0,fd,75,fe,1,75,ff,2,85,d0,fd,75,fe,0,75,ff,2,75,e0,1,75,
  //   f0,fe,84,85,e0,fd,75,fe,0,75,ff,2,85,f0,fd,75,fe,1,75,ff,2,85,d0,fd,75,fe,0,75,ff,
  //   2,75,e0,1,75,f0,ff,84,85,e0,fd,75,fe,0,75,ff,2,85,f0,fd,75,fe,1,75,ff,2,85,d0,fd,
  //   75,fe,0,75,ff,2,75,e0,2,75,f0,0,84,85,d0,fd,75,fe,5,75,ff,2,75,e0,2,75,f0,1,84,85,
  //   e0,fd,75,fe,2,75,ff,2,85,f0,fd,75,fe,0,75,ff,2,85,d0,fd,75,fe,1,75,ff,2,75,e0,2,75,
  //   f0,2,84,85,e0,fd,75,fe,1,75,ff,2,85,f0,fd,75,fe,0,75,ff,2,85,d0,fd,75,fe,1,75,ff,
  //   2,75,e0,2,75,f0,3,84,85,e0,fd,75,fe,0,75,ff,2,85,f0,fd,75,fe,2,75,ff,2,85,d0,fd,75,
  //   fe,0,75,ff,2,75,e0,2,75,f0,7c,84,85,e0,fd,75,fe,0,75,ff,2,85,f0,fd,75,fe,2,75,ff,
  //   2,85,d0,fd,75,fe,0,75,ff,2,75,e0,2,75,f0,7d,84,85,e0,fd,75,fe,0,75,ff,2,85,f0,fd,
  //   75,fe,2,75,ff,2,85,d0,fd,75,fe,0,75,ff,2,75,e0,2,75,f0,7e,84,85,e0,fd,75,fe,0,75,
  //   ff,2,85,f0,fd,75,fe,2,75,ff,2,85,d0,fd,75,fe,0,75,ff,2,75,e0,2,75,f0,7f,84,85,e0,
  //   fd,75,fe,0,75,ff,2,85,f0,fd,75,fe,2,75,ff,2,85,d0,fd,75,fe,0,75,ff,2,75,e0,2,75,f0,
  //   80,84,85,e0,fd,75,fe,0,75,ff,2,85,f0,fd,75,fe,2,75,ff,2,85,d0,fd,75,fe,0,75,ff,2,
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endmodule
