// Digital circuit TOP.dig as structural Verilog
module TOP (
  input  clk,
  input  [11:0] MIPCBI,
  input  MIPCBE,
  input  [15:0] PCBIA1,
  input  PCBE1,
  input  [15:0] PCBIA2,
  input  PCBE2
);

  wire and_1_out, and_2_out, and_3_out, button_1_out, button_2_out, button_3_out, button_4_out,
       comparator_1_eq, comparator_2_eq, comparator_3_eq, dipswitch_1_out, or_1_out;
  wire [11:0] MIPC;
  wire [15:0] PC;

  Comparator #(.Bits(12)) comparator_1 (.a(MIPCBI), .b(MIPC), .eq(comparator_1_eq));  // open: gt, lt
  Comparator #(.Bits(16)) comparator_2 (.a(PCBIA1), .b(PC), .eq(comparator_2_eq));  // open: gt, lt
  Comparator #(.Bits(16)) comparator_3 (.a(PCBIA2), .b(PC), .eq(comparator_3_eq));  // open: gt, lt
  and and_1 (and_1_out, comparator_1_eq, MIPCBE);
  and and_2 (and_2_out, comparator_2_eq, PCBE1);
  and and_3 (and_3_out, comparator_3_eq, PCBE2);
  DipSwitch dipswitch_1 (.out(dipswitch_1_out));
  Button button_1 (.out(button_1_out));
  Button button_2 (.out(button_2_out));
  Button button_3 (.out(button_3_out));
  Button button_4 (.out(button_4_out));
  or or_1 (or_1_out, and_1_out, and_2_out, and_3_out);
  // CORE core_1: pin names not known; wires that end beside it: clk, button_1_out, dipswitch_1_out, button_2_out, button_3_out, button_4_out, or_1_out, PC, MIPC
  // Probe on PC
  // Probe on MIPC

  // Notes on the sheet:
  //   clk: Hz: 2147483647
endmodule
